# Fritzing sketch Sketch_2.0 (saved by Fritzing 0.9.3b)
breadboards: 1

parts:
  Bauteil1 = Arduino Uno (Rev3)
  R1 = Resistor [tolerance=±5% resistance=10k package=THT]
  3-pins_Hall_Effect_Sensor1 = mystery part, 3 pins [chip_label=Hall]
  J1 = Basic Servo

nets:
  N1: Bauteil1.D9_PWM, J1.pulse
  N2: Bauteil1.D2, R1.Pin_1, 3-pins_Hall_Effect_Sensor1.pin3
  N3: Bauteil1.3V3, R1.Pin_0, 3-pins_Hall_Effect_Sensor1.pin1
  5V: Bauteil1.5V, J1.vcc
  GND: Bauteil1.GND, 3-pins_Hall_Effect_Sensor1.pin2, J1.gnd
